// Logisim project ex2.circ as structural Verilog: 1 circuit, main circuit compute_BrUn
module compute_BrUn (
  input  [31:0] INSTRUCTION,
  output BrUn
);

  wire comparator_1_eq, comparator_2_eq, comparator_3_eq, comparator_4_eq, is_bgeu, is_bltu, or_1_out;

  Comparator #(.width(7)) comparator_1 (.a(INSTRUCTION[6:0]), .b(7'b1100011), .eq(comparator_1_eq));  // open: gt, lt
  Comparator #(.width(3)) comparator_2 (.a(INSTRUCTION[14:12]), .b(3'b110), .eq(comparator_2_eq));  // open: gt, lt
  Comparator #(.width(7)) comparator_3 (.a(INSTRUCTION[6:0]), .b(7'b1100011), .eq(comparator_3_eq));  // open: gt, lt
  Comparator #(.width(3)) comparator_4 (.a(INSTRUCTION[14:12]), .b(3'b111), .eq(comparator_4_eq));  // open: gt, lt
  and and_1 (is_bltu, comparator_1_eq, comparator_2_eq);
  and and_2 (is_bgeu, comparator_3_eq, comparator_4_eq);
  Multiplexer multiplexer_1 (.in0(1'b0), .in1(1'b1), .out(BrUn), .sel(or_1_out));
  or or_1 (or_1_out, is_bltu, is_bgeu);

  // Other names for the same wires on the sheet: opcode[6:0] = INSTRUCTION[6:0]; funct3[2:0] = INSTRUCTION[14:12];
  //   funct7[6:0] = INSTRUCTION[31:25]
endmodule
