// Logisim project cpu.circ as structural Verilog: 1 circuit, main circuit cpu
module cpu (
  input  clk,
  input  [31:0] Instruction,
  input  [31:0] MemReadData,
  output [31:0] MemAddress,
  output [31:0] ProgramCounter,
  output [31:0] ra,
  output [31:0] sp,
  output [31:0] t0,
  output [31:0] t1,
  output [31:0] t2,
  output [31:0] s0,
  output [31:0] s1,
  output [31:0] a0,
  output [3:0] MemWriteMask,
  output [31:0] MemWriteData
);

  wire ASel, BrEq, BrLt, BrUn, BSel, control_logic_1_regwen, MemRW, PCsel;
  wire [1:0] WBSel;
  wire [2:0] control_logic_1_immsel;
  wire [3:0] ALUSel;
  wire [31:0] EX_Instruction, EX_PC, EX_PC4, IF_PC4, Immediate, multiplexer_1_out, multiplexer_2_out,
       multiplexer_4_out, multiplexer_5_out, partial_load_1_datatoreg, ReadData1, ReadData2, wdata;

  Adder #(.width(32)) adder_1 (.a(ProgramCounter), .b(32'h4), .out(IF_PC4));  // open: cin, cout
  Multiplexer #(.width(32)) multiplexer_1 (.in0(IF_PC4), .in1(MemAddress), .out(multiplexer_1_out), .sel(PCsel));
  Register #(.width(32)) IF_EX_PC (.D(ProgramCounter), .clk(clk), .Q(EX_PC));  // open: en, clr
  Register #(.width(32)) register_1 (.D(IF_PC4), .clk(clk), .Q(EX_PC4));  // open: en, clr
  Register #(.width(32)) PC (.D(multiplexer_1_out), .clk(clk), .Q(ProgramCounter));  // open: en, clr
  Register #(.width(32)) register_2 (.D(multiplexer_2_out), .clk(clk), .Q(EX_Instruction));  // open: en, clr
  Multiplexer #(.width(32)) multiplexer_2 (.in0(Instruction), .in1(32'h13), .out(multiplexer_2_out), .sel(PCsel));
  control_logic control_logic_1 (
    .Instruction(EX_Instruction), .BrEq(BrEq), .BrLt(BrLt), .PCSel(PCsel), .RegWEn(control_logic_1_regwen),
    .ImmSel(control_logic_1_immsel), .BrUn(BrUn), .ASel(ASel), .BSel(BSel), .ALUSel(ALUSel), .MemRW(MemRW),
    .WBSel(WBSel));
  regfile regfile_1 (
    .ReadIndex1(EX_Instruction[19:15]), .ReadIndex2(EX_Instruction[24:20]),
    .WriteIndex(EX_Instruction[11:7]), .WriteData(wdata), .RegWEn(control_logic_1_regwen), .clk(clk),
    .ra(ra), .sp(sp), .t0(t0), .t1(t1), .t2(t2), .s0(s0), .s1(s1), .a0(a0), .ReadData1(ReadData1),
    .ReadData2(ReadData2));
  partial_load partial_load_1 (
    .Instruction(EX_Instruction), .MemAddress(MemAddress), .DataFromMem(MemReadData),
    .DataToReg(partial_load_1_datatoreg));
  partial_store partial_store_1 (
    .Instruction(EX_Instruction), .MemAddress(MemAddress), .DataFromReg(ReadData2), .MemRW(MemRW),
    .MemWriteMask(MemWriteMask), .DataToMem(MemWriteData));
  imm_gen imm_gen_1 (.Instruction(EX_Instruction), .ImmSel(control_logic_1_immsel), .Immediate(Immediate));
  Multiplexer #(.select(2), .width(32)) multiplexer_3 (
    .in0(partial_load_1_datatoreg), .in1(MemAddress), .in2(EX_PC4), .out(wdata), .sel(WBSel));  // open: in3
  Multiplexer #(.width(32)) multiplexer_4 (.in0(ReadData1), .in1(EX_PC), .out(multiplexer_4_out), .sel(ASel));
  Multiplexer #(.width(32)) multiplexer_5 (.in0(ReadData2), .in1(Immediate), .out(multiplexer_5_out), .sel(BSel));
  alu alu_1 (.A(multiplexer_4_out), .B(multiplexer_5_out), .ALUSel(ALUSel), .ALUResult(MemAddress));
  branch_comp branch_comp_1 (.BrData1(ReadData1), .BrData2(ReadData2), .BrUn(BrUn), .BrEq(BrEq), .BrLt(BrLt));

  // Other names for the same wires on the sheet: alu_out[31:0] = MemAddress; IF_Instruction[31:0] = Instruction;
  //   IF_PC[31:0] = ProgramCounter

  // Notes on the sheet:
  //   To IMEM
  //   IMEM (do **NOT** move this)
  //   From IMEM
  //   Inputs/Outputs for testing. Do **NOT** move these.
  //   It is OK to move the PC, RegFile, ALU, MEM, Branch Comp, Imm Gen, Partial Load, Partial Store and Control Logic to wherever is most convenient for you when constructing your CPU, and to delete this text
  //   To DMEM
  //   DMEM (do **NOT** move this)
  //   From DMEM
endmodule
