// Logisim project imm-gen.circ as structural Verilog: 1 circuit, main circuit imm_gen
module imm_gen (
  input  [31:0] Instruction,
  input  [2:0] ImmSel,
  output [31:0] Immediate
);

  wire [31:0] bit_extender_4_out, Utype;
  wire [31:11] Itype, Stype;
  wire [31:12] Btype;
  wire [31:20] Jtype;

  assign Btype = {{19{Instruction[31]}}, Instruction[31]};  // Bit_Extender bit_extender_1
  assign Itype = {{20{Instruction[31]}}, Instruction[31]};  // Bit_Extender bit_extender_2
  assign Stype = {{20{Instruction[31]}}, Instruction[31]};  // Bit_Extender bit_extender_3
  assign bit_extender_4_out = {{12{1'b0}}, Instruction[31:12]};  // Bit_Extender bit_extender_4
  assign Jtype = {{11{Instruction[31]}}, Instruction[31]};  // Bit_Extender bit_extender_5
  Shifter #(.width(32)) shifter_1 (.in(bit_extender_4_out), .\dist (5'b01100), .out(Utype));
  Multiplexer #(.select(3), .width(32)) multiplexer_1 (
    .in0({Itype, Instruction[30:20]}), .in1({Stype, Instruction[30:25], Instruction[11:7]}),
    .in2({Btype, Instruction[7], Instruction[30:25], Instruction[11:8], 1'b0}), .in3(Utype),
    .in4({Jtype, Instruction[19:12], Instruction[20], Instruction[30:21], 1'b0}), .out(Immediate),
    .sel(ImmSel));  // open: in5, in6, in7

  // Other names for the same wires on the sheet: Itype[10:0] = Instruction[30:20];
  //   Jtype[19:1] = {Instruction[19:12], Instruction[20], Instruction[30:21]};
  //   Btype[11:1] = {Instruction[7], Instruction[30:25], Instruction[11:8]};
  //   Stype[10:0] = {Instruction[30:25], Instruction[11:7]}

  // Notes on the sheet:
  //   INPUTS to your circuit
  //   DON'T CHANGE THE LOCATIONS OF THE INPUTS AND OUTPUTS!
  //   OUTPUT from your circuit
endmodule
