// Logisim project partial-store.circ as structural Verilog: 1 circuit, main circuit partial_store
module partial_store (
  input  [31:0] Instruction,
  input  [31:0] MemAddress,
  input  [31:0] DataFromReg,
  input  MemRW,
  output [3:0] MemWriteMask,
  output [31:0] DataToMem
);

  wire [1:0] and_1_out;
  wire [3:0] multiplexer_6_out, sb_mask, sh_mask;
  wire [31:0] multiplexer_5_out, sb_data, sh_data;

  Multiplexer #(.select(2), .width(4)) multiplexer_1 (
    .in0(4'b0001), .in1(4'b0010), .in2(4'b0100), .in3(4'b1000), .out(sb_mask), .sel(MemAddress[1:0]));
  assign and_1_out = MemAddress[1:0] & 2'b10;  // AND_Gate and_1, 2 bits wide
  Multiplexer #(.select(2), .width(4)) multiplexer_2 (
    .in0(4'b0011), .in2(4'b1100), .out(sh_mask), .sel(MemAddress[1:0]));  // open: in1, in3
  Multiplexer #(.select(2), .width(32)) multiplexer_3 (
    .in0({{24{1'b0}}, DataFromReg[7:0]}), .in1({{16{1'b0}}, DataFromReg[7:0], {8{1'b0}}}),
    .in2({{8{1'b0}}, DataFromReg[7:0], {16{1'b0}}}), .in3({DataFromReg[7:0], {24{1'b0}}}), .out(sb_data),
    .sel(MemAddress[1:0]));
  Multiplexer #(.select(2), .width(32)) multiplexer_4 (
    .in0({{16{1'b0}}, DataFromReg[15:0]}), .in2({DataFromReg[15:0], {16{1'b0}}}), .out(sh_data),
    .sel(and_1_out));  // open: in1, in3
  Multiplexer #(.select(3), .width(32)) multiplexer_5 (
    .in0(sb_data), .in1(sh_data), .in2(DataFromReg), .out(multiplexer_5_out), .sel(Instruction[14:12]));  // open: in3, in4, in5, in6, in7
  Multiplexer #(.select(3), .width(4)) multiplexer_6 (
    .in0(sb_mask), .in1(sh_mask), .in2(4'b1111), .out(multiplexer_6_out), .sel(Instruction[14:12]));  // open: in3, in4, in5, in6, in7
  Multiplexer #(.width(4)) multiplexer_7 (.in0(4'b0000), .in1(multiplexer_6_out), .out(MemWriteMask), .sel(MemRW));
  assign DataToMem = multiplexer_5_out | {32{1'b0}};  // OR_Gate or_1, 32 bits wide

  // Other names for the same wires on the sheet: ByteData[7:0] = DataFromReg[7:0];
  //   HalfwordData[15:0] = DataFromReg[15:0]; sw_data[31:0] = DataFromReg; WordData[31:0] = DataFromReg;
  //   func3[2:0] = Instruction[14:12]; addr2[1:0] = MemAddress[1:0]

  // Notes on the sheet:
  //   INPUTS to your circuit
  //   DON'T CHANGE THE LOCATIONS OF THE INPUTS AND OUTPUTS!
  //   OUTPUT from your circuit
endmodule
