// Logisim project regfile.circ as structural Verilog: 1 circuit, main circuit regfile
module regfile (
  input  [4:0] ReadIndex1,
  input  [4:0] ReadIndex2,
  input  [4:0] WriteIndex,
  input  [31:0] WriteData,
  input  RegWEn,
  input  clk,
  output [31:0] ra,
  output [31:0] sp,
  output [31:0] t0,
  output [31:0] t1,
  output [31:0] t2,
  output [31:0] s0,
  output [31:0] s1,
  output [31:0] a0,
  output [31:0] ReadData1,
  output [31:0] ReadData2
);

  wire RegWEn0, RegWEn1, RegWEn2, RegWEn3, RegWEn4, RegWEn5, RegWEn6, RegWEn7, RegWEn8, RegWEn9, RegWEn10,
       RegWEn11, RegWEn12, RegWEn13, RegWEn14, RegWEn15, RegWEn16, RegWEn17, RegWEn18, RegWEn19, RegWEn20,
       RegWEn21, RegWEn22, RegWEn23, RegWEn24, RegWEn25, RegWEn26, RegWEn27, RegWEn28, RegWEn29, RegWEn30,
       RegWEn31;
  wire [31:0] ReadData3, ReadData4, ReadData11, ReadData12, ReadData13, ReadData14, ReadData15, ReadData16,
       ReadData17, ReadData18, ReadData19, ReadData20, ReadData21, ReadData22, ReadData23, ReadData24,
       ReadData25, ReadData26, ReadData27, ReadData28, ReadData29, ReadData30, ReadData31;

  Register #(.width(32)) x0 (.en(RegWEn0), .clk(clk));  // open: D, Q, clr
  Register #(.width(32)) x1 (.D(WriteData), .en(RegWEn1), .clk(clk), .Q(ra));  // open: clr
  Register #(.width(32)) x2 (.D(WriteData), .en(RegWEn2), .clk(clk), .Q(sp));  // open: clr
  Register #(.width(32)) x3 (.D(WriteData), .en(RegWEn3), .clk(clk), .Q(ReadData3));  // open: clr
  Register #(.width(32)) x4 (.D(WriteData), .en(RegWEn4), .clk(clk), .Q(ReadData4));  // open: clr
  Register #(.width(32)) x5 (.D(WriteData), .en(RegWEn5), .clk(clk), .Q(t0));  // open: clr
  Register #(.width(32)) x6 (.D(WriteData), .en(RegWEn6), .clk(clk), .Q(t1));  // open: clr
  Register #(.width(32)) x7 (.D(WriteData), .en(RegWEn7), .clk(clk), .Q(t2));  // open: clr
  Register #(.width(32)) x8 (.D(WriteData), .en(RegWEn8), .clk(clk), .Q(s0));  // open: clr
  Register #(.width(32)) x9 (.D(WriteData), .en(RegWEn9), .clk(clk), .Q(s1));  // open: clr
  Register #(.width(32)) x10 (.D(WriteData), .en(RegWEn10), .clk(clk), .Q(a0));  // open: clr
  Register #(.width(32)) x11 (.D(WriteData), .en(RegWEn11), .clk(clk), .Q(ReadData11));  // open: clr
  Register #(.width(32)) x12 (.D(WriteData), .en(RegWEn12), .clk(clk), .Q(ReadData12));  // open: clr
  Register #(.width(32)) x13 (.D(WriteData), .en(RegWEn13), .clk(clk), .Q(ReadData13));  // open: clr
  Register #(.width(32)) x14 (.D(WriteData), .en(RegWEn14), .clk(clk), .Q(ReadData14));  // open: clr
  Register #(.width(32)) x15 (.D(WriteData), .en(RegWEn15), .clk(clk), .Q(ReadData15));  // open: clr
  Register #(.width(32)) x16 (.D(WriteData), .en(RegWEn16), .clk(clk), .Q(ReadData16));  // open: clr
  Register #(.width(32)) x17 (.D(WriteData), .en(RegWEn17), .clk(clk), .Q(ReadData17));  // open: clr
  Register #(.width(32)) x18 (.D(WriteData), .en(RegWEn18), .clk(clk), .Q(ReadData18));  // open: clr
  Register #(.width(32)) x19 (.D(WriteData), .en(RegWEn19), .clk(clk), .Q(ReadData19));  // open: clr
  Register #(.width(32)) x20 (.D(WriteData), .en(RegWEn20), .clk(clk), .Q(ReadData20));  // open: clr
  Register #(.width(32)) x21 (.D(WriteData), .en(RegWEn21), .clk(clk), .Q(ReadData21));  // open: clr
  Register #(.width(32)) x22 (.D(WriteData), .en(RegWEn22), .clk(clk), .Q(ReadData22));  // open: clr
  Register #(.width(32)) x23 (.D(WriteData), .en(RegWEn23), .clk(clk), .Q(ReadData23));  // open: clr
  Register #(.width(32)) x24 (.D(WriteData), .en(RegWEn24), .clk(clk), .Q(ReadData24));  // open: clr
  Register #(.width(32)) x25 (.D(WriteData), .en(RegWEn25), .clk(clk), .Q(ReadData25));  // open: clr
  Register #(.width(32)) x26 (.D(WriteData), .en(RegWEn26), .clk(clk), .Q(ReadData26));  // open: clr
  Register #(.width(32)) x27 (.D(WriteData), .en(RegWEn27), .clk(clk), .Q(ReadData27));  // open: clr
  Register #(.width(32)) x28 (.D(WriteData), .en(RegWEn28), .clk(clk), .Q(ReadData28));  // open: clr
  Register #(.width(32)) x29 (.D(WriteData), .en(RegWEn29), .clk(clk), .Q(ReadData29));  // open: clr
  Register #(.width(32)) x30 (.D(WriteData), .en(RegWEn30), .clk(clk), .Q(ReadData30));  // open: clr
  Register #(.width(32)) x31 (.D(WriteData), .en(RegWEn31), .clk(clk), .Q(ReadData31));  // open: clr
  Demultiplexer #(.select(5)) demultiplexer_1 (
    .out0(RegWEn0), .out1(RegWEn1), .out2(RegWEn2), .out3(RegWEn3), .out4(RegWEn4), .out5(RegWEn5),
    .out6(RegWEn6), .out7(RegWEn7), .out8(RegWEn8), .out9(RegWEn9), .out10(RegWEn10), .out11(RegWEn11),
    .out12(RegWEn12), .out13(RegWEn13), .out14(RegWEn14), .out15(RegWEn15), .out16(RegWEn16),
    .out17(RegWEn17), .out18(RegWEn18), .out19(RegWEn19), .out20(RegWEn20), .out21(RegWEn21),
    .out22(RegWEn22), .out23(RegWEn23), .out24(RegWEn24), .out25(RegWEn25), .out26(RegWEn26),
    .out27(RegWEn27), .out28(RegWEn28), .out29(RegWEn29), .out30(RegWEn30), .out31(RegWEn31), .in(RegWEn),
    .sel(WriteIndex));
  Multiplexer #(.select(5), .width(32)) multiplexer_1 (
    .in0({32{1'b0}}), .in1(ra), .in2(sp), .in3(ReadData3), .in4(ReadData4), .in5(t0), .in6(t1), .in7(t2),
    .in8(s0), .in9(s1), .in10(a0), .in11(ReadData11), .in12(ReadData12), .in13(ReadData13),
    .in14(ReadData14), .in15(ReadData15), .in16(ReadData16), .in17(ReadData17), .in18(ReadData18),
    .in19(ReadData19), .in20(ReadData20), .in21(ReadData21), .in22(ReadData22), .in23(ReadData23),
    .in24(ReadData24), .in25(ReadData25), .in26(ReadData26), .in27(ReadData27), .in28(ReadData28),
    .in29(ReadData29), .in30(ReadData30), .in31(ReadData31), .out(ReadData1), .sel(ReadIndex1));
  Multiplexer #(.select(5), .width(32)) multiplexer_2 (
    .in0({32{1'b0}}), .in1(ra), .in2(sp), .in3(ReadData3), .in4(ReadData4), .in5(t0), .in6(t1), .in7(t2),
    .in8(s0), .in9(s1), .in10(a0), .in11(ReadData11), .in12(ReadData12), .in13(ReadData13),
    .in14(ReadData14), .in15(ReadData15), .in16(ReadData16), .in17(ReadData17), .in18(ReadData18),
    .in19(ReadData19), .in20(ReadData20), .in21(ReadData21), .in22(ReadData22), .in23(ReadData23),
    .in24(ReadData24), .in25(ReadData25), .in26(ReadData26), .in27(ReadData27), .in28(ReadData28),
    .in29(ReadData29), .in30(ReadData30), .in31(ReadData31), .out(ReadData2), .sel(ReadIndex2));

  // Other names for the same wires on the sheet: ReadData01[31:0] = ReadData1; ReadData1_t[31:0] = ra;
  //   ReadData02[31:0] = ReadData2; ReadData2_t[31:0] = sp; ReadData5[31:0] = t0; ReadData6[31:0] = t1;
  //   ReadData7[31:0] = t2; ReadData8[31:0] = s0; ReadData9[31:0] = s1; ReadData10[31:0] = a0

  // Notes on the sheet:
  //   INPUTS to your circuit
  //   DON'T CHANGE THE LOCATIONS OF THE INPUTS AND OUTPUTS!
  //   These are DEBUG/TEST outputs from your circuit.
  //   OUTPUTS from your circuit
endmodule
